// Logisim project DOE SHIFT REGISTER ENCODER DECODER.circ as structural Verilog
module main (
  input  in_1,
  input  in_2,
  output BINARY,
  output out_4,
  output out_5,
  output out_6
);

  wire and_1_out, and_2_out, button_1_out, clock_1_out, d_ff_1_q, d_ff_2_q, d_ff_3_q, d_ff_4_q, d_ff_5_q,
       d_ff_6_q, d_ff_7_q, d_ff_7_qn, d_ff_8_q, d_ff_9_q, d_ff_9_qn, d_ff_10_q, d_ff_11_q, d_ff_12_q,
       d_ff_13_q, d_ff_14_q, d_ff_15_q, d_ff_16_q, d_ff_17_q, decoder_1_a, decoder_1_b, decoder_1_c,
       decoder_1_d, decoder_1_e, decoder_1_f, decoder_1_g, or_1_out;

  Clock clock_1 (.out(clock_1_out));
  Button button_1 (.out(button_1_out));
  and and_1 (and_1_out, ~d_ff_7_q, ~d_ff_6_q, ~d_ff_4_q, ~d_ff_2_q, ~d_ff_1_q);  // AND_Gate
  or or_1 (or_1_out, and_1_out, button_1_out);
  D_Flip_Flop d_ff_1 (.clk(clock_1_out), .D(d_ff_7_qn), .Q(d_ff_1_q), .reset(button_1_out));  // open: Qn, preset, en
  and and_2 (and_2_out, in_1, in_2);
  D_Flip_Flop d_ff_2 (.clk(clock_1_out), .D(d_ff_1_q), .Q(d_ff_2_q), .reset(button_1_out));  // open: Qn, preset, en
  D_Flip_Flop d_ff_3 (.clk(and_2_out), .D(d_ff_9_qn), .Q(d_ff_3_q), .reset(or_1_out));  // open: Qn, preset, en
  D_Flip_Flop d_ff_4 (.clk(clock_1_out), .D(d_ff_2_q), .Q(d_ff_4_q), .reset(button_1_out));  // open: Qn, preset, en
  D_Flip_Flop d_ff_5 (.clk(and_2_out), .D(d_ff_3_q), .Q(d_ff_5_q), .reset(or_1_out));  // open: Qn, preset, en
  encoder encoder_1 (
    .A(d_ff_3_q), .B(d_ff_5_q), .C(d_ff_8_q), .D(d_ff_10_q), .E(d_ff_9_q), .T(BINARY), .U(out_4), .V(out_5),
    .X(out_6));
  D_Flip_Flop d_ff_6 (.clk(clock_1_out), .D(d_ff_4_q), .Q(d_ff_6_q), .reset(button_1_out));  // open: Qn, preset, en
  D_Flip_Flop d_ff_7 (
    .clk(clock_1_out), .D(d_ff_6_q), .Q(d_ff_7_q), .Qn(d_ff_7_qn), .reset(button_1_out));  // open: preset, en
  D_Flip_Flop d_ff_8 (.clk(and_2_out), .D(d_ff_5_q), .Q(d_ff_8_q), .reset(or_1_out));  // open: Qn, preset, en
  decoder decoder_1 (
    .T(BINARY), .U(out_4), .V(out_5), .X(out_6), .a(decoder_1_a), .b(decoder_1_b), .c(decoder_1_c),
    .d(decoder_1_d), .e(decoder_1_e), .f(decoder_1_f), .g(decoder_1_g));
  D_Flip_Flop d_ff_9 (.clk(and_2_out), .D(d_ff_10_q), .Q(d_ff_9_q), .Qn(d_ff_9_qn));  // open: preset, en, reset
  D_Flip_Flop d_ff_10 (.clk(and_2_out), .D(d_ff_8_q), .Q(d_ff_10_q), .reset(or_1_out));  // open: Qn, preset, en
  _7_Segment_Display u_7_segment_display_1 (
    .g(d_ff_17_q), .f(d_ff_16_q), .a(d_ff_11_q), .b(d_ff_12_q), .e(d_ff_15_q), .d(d_ff_14_q), .c(d_ff_13_q));  // open: dp
  D_Flip_Flop d_ff_11 (.clk(or_1_out), .D(decoder_1_a), .Q(d_ff_11_q), .reset(button_1_out));  // open: Qn, preset, en
  D_Flip_Flop d_ff_12 (.clk(or_1_out), .D(decoder_1_b), .Q(d_ff_12_q), .reset(button_1_out));  // open: Qn, preset, en
  D_Flip_Flop d_ff_13 (.clk(or_1_out), .D(decoder_1_c), .Q(d_ff_13_q), .reset(button_1_out));  // open: Qn, preset, en
  D_Flip_Flop d_ff_14 (.clk(or_1_out), .D(decoder_1_d), .Q(d_ff_14_q), .reset(button_1_out));  // open: Qn, preset, en
  D_Flip_Flop d_ff_15 (.clk(or_1_out), .D(decoder_1_e), .Q(d_ff_15_q), .reset(button_1_out));  // open: Qn, preset, en
  D_Flip_Flop d_ff_16 (.clk(or_1_out), .D(decoder_1_f), .Q(d_ff_16_q), .reset(button_1_out));  // open: Qn, preset, en
  D_Flip_Flop d_ff_17 (.clk(or_1_out), .D(decoder_1_g), .Q(d_ff_17_q), .reset(button_1_out));  // open: Qn, preset, en

  // Notes on the sheet:
  //   THIS COUNTS OR INCREMENTS WHEN BOTH CONDITIONS ARE SATISFIED
endmodule

// AHI DEC
module decoder (
  input  T,
  input  U,
  input  V,
  input  X,
  output a,
  output b,
  output c,
  output d,
  output e,
  output f,
  output g
);

  wire and_1_out, and_2_out, and_3_out, and_4_out, not_1_out, not_2_out, not_3_out, not_4_out, not_5_out,
       not_6_out, not_7_out, not_8_out, not_9_out, not_10_out;

  or or_1 (a, U, T);
  not not_1 (not_1_out, U);
  or or_2 (c, not_1_out, T);
  not not_2 (not_2_out, V);
  and and_1 (and_1_out, not_2_out, not_3_out);
  not not_3 (not_3_out, X);
  not not_4 (not_4_out, T);
  not not_5 (not_5_out, V);
  and and_2 (and_2_out, not_4_out, not_5_out, not_6_out);
  not not_6 (not_6_out, X);
  not not_7 (not_7_out, T);
  not not_8 (not_8_out, U);
  not not_9 (not_9_out, V);
  not not_10 (not_10_out, X);
  or or_3 (g, U, T);
  or or_4 (d, and_1_out, U, T);
  or or_5 (e, and_2_out, U);
  and and_3 (and_3_out, not_7_out, not_8_out, not_9_out, not_10_out);
  or or_6 (f, and_3_out, and_4_out);
  and and_4 (and_4_out, T, U);

  assign b = 1'b1;
endmodule

// ENC
module encoder (
  input  A,
  input  B,
  input  C,
  input  D,
  input  E,
  output T,
  output U,
  output V,
  output X
);

  wire and_1_out, and_2_out, and_3_out, and_4_out, and_5_out, and_6_out, and_7_out, and_8_out, and_9_out,
       and_10_out, and_11_out;

  and and_1 (and_1_out, ~A, ~B, ~C, E);  // AND_Gate
  buf or_1 (T, and_1_out);  // OR_Gate
  and and_2 (and_2_out, A, B, C, D);
  and and_3 (and_3_out, ~A, C, D, E);  // AND_Gate
  or or_2 (U, and_3_out, and_2_out);
  and and_4 (and_4_out, A, B, ~D, ~E);  // AND_Gate
  or or_3 (V, and_3_out, and_4_out);
  and and_5 (and_5_out, ~A, ~B, ~C, ~D, ~E);  // AND_Gate
  and and_6 (and_6_out, A, ~B, ~C, ~D, ~E);  // AND_Gate
  and and_7 (and_7_out, ~A, ~B, C, D, E);  // AND_Gate
  or or_4 (X, and_7_out, and_6_out, and_8_out, and_9_out);
  and and_8 (and_8_out, A, B, C, ~D, ~E);  // AND_Gate
  and and_9 (and_9_out, A, B, C, D, E);
  and and_10 (and_10_out, ~A, ~B, ~C, ~D, E);  // AND_Gate
  and and_11 (and_11_out, ~A, ~B, ~C, ~D);  // AND_Gate

  // Notes on the sheet:
  //   T = A'B'C'E
  //   U = A'CDE + ABCD
  //   V = A'CDE + ABD'E' + A'B'C'D'E
  //   X =A'B'CDE + AB'C'D'E' + ABCD'E' + ABCDE
endmodule
